# Fritzing sketch SequencialSwitch (saved by Fritzing 0.9.3b)
stripboards: 1

parts:
  Q1 = NPN-Transistor [part_number=3904 package="TO92 [THT]"]
  Q2 = NPN-Transistor [part_number=3904 package="TO92 [THT]"]
  R2 = Vertical Resistor [tolerance=±1% resistance=10k package=THT]
  R3 = Vertical Resistor [tolerance=±1% resistance=10k package=THT]
  ClockLED = Diode [part_number=1N4148 package=diode-1n4148]
  R4 = Vertical Resistor [tolerance=±1% resistance=47k package=THT]
  Q3 = NPN-Transistor [part_number=3904 package="TO92 [THT]"]
  Q4 = NPN-Transistor [part_number=3904 package="TO92 [THT]"]
  R5 = Vertical Resistor [tolerance=±1% resistance=10k package=THT]
  R6 = Vertical Resistor [tolerance=±1% resistance=47k package=THT]
  R7 = Vertical Resistor [tolerance=±1% resistance=10k package=THT]
  ResetLED = Diode [part_number=1N4148 package=diode-1n4148]
  J8 = female pin header, 1 pin [form="♀ (female)" part_number="gnd point"]
  J9 = female pin header, 5 pins [form="♀ (female)"]
  -_GND_+1 = female pin header, 5 pins [form="♀ (female)"]
  C23 = Electrolytic Capacitor [capacitance=47µF voltage=35V package="100 mil [THT, electrolytic]"]
  C24 = Electrolytic Capacitor [capacitance=47µF voltage=35V package="100 mil [THT, electrolytic]"]
  C25 = Ceramic Capacitor [capacitance=10nF voltage=35V package="100 mil [THT, multilayer]"]
  C26 = Ceramic Capacitor [capacitance=10nF voltage=35V package="100 mil [THT, multilayer]"]
  SW3 = Toggle Switch [part_number="3 position switch" package=THT]
  D8 = Diode [package=diode-1n4148]
  R8 = Resistor [tolerance=±1% resistance=47k package=THT]
  R1 = Resistor [tolerance=±1% resistance=47k package=THT]
  R9 = Resistor [tolerance=±1% resistance=1k package=THT]
  R10 = Resistor [tolerance=±1% resistance=1k package=THT]
  R11 = Resistor [tolerance=±1% resistance=1k package=THT]
  R12 = Resistor [tolerance=±1% resistance=1k package=THT]
  R13 = Resistor [tolerance=±1% resistance=1k package=THT]
  D3 = Diode [package=diode-1n4148]
  C27 = Ceramic Capacitor [capacitance=10nF voltage=35V package="100 mil [THT, multilayer]"]
  R14 = Resistor [tolerance=±1% resistance=1k package=THT]
  manStepLED = Diode [part_number=1N4148 package=diode-1n4148]
  C28 = Ceramic Capacitor [capacitance=100nF voltage=35V package="100 mil [THT, multilayer]"]
  R15 = Resistor [tolerance=±1% resistance=1k package=THT]
  manResetLED = Diode [part_number=1N4148 package=diode-1n4148]
  C29 = Ceramic Capacitor [capacitance=100nF voltage=35V package="100 mil [THT, multilayer]"]
  S1 = Momentary Switch [part_number=stepSW package=tactile_switch_smd]
  S2 = Momentary Switch [part_number=resetSW package=tactile_switch_smd]
  IC2 = SO16 [chip_label=DG412 part_number=DG412 package=SO]
  IC1 = SO16 [chip_label=4017 part_number=CD4017 package=SO]
  Reset = 3.5mm Switch Jack [part_number=PJ301M-12]
  Step = 3.5mm Switch Jack [part_number=PJ301M-12]
  OI = 3.5mm Switch Jack [part_number=PJ301M-12]
  IO1 = 3.5mm Switch Jack [part_number=PJ301M-12]
  IO2 = 3.5mm Switch Jack [part_number=PJ301M-12]
  IO3 = 3.5mm Switch Jack [part_number=PJ301M-12]
  IO4 = 3.5mm Switch Jack [part_number=PJ301M-12]
  D1 = Diode [part_number=1N5819WS package=sod-323]
  D2 = Diode [part_number=1N5819WS package=sod-323]

nets:
  GND: Q1.E, Q2.E, R4.Pin_1, Q3.E, Q4.E, R6.Pin_1, J8.pin1, J9.pin2, J9.pin3, J9.pin4, -_GND_+1.pin2, -_GND_+1.pin3, -_GND_+1.pin4, C23.+, C24.-, C25.0, C26.0, C27.0, C28.1, C29.1, IC2.5, IC1.8, IC1.13, Reset.Pin_1, Step.Pin_1, OI.Pin_1, IO1.Pin_1, IO2.Pin_1, IO3.Pin_1, IO4.Pin_1
  N1: Q1.B, Q2.C, R2.Pin_1
  N2: Q1.C, R3.Pin_1, ClockLED.A
  N3: Q2.B, R1.Pin_1
  12V: R2.Pin_0, R3.Pin_0, R5.Pin_0, R7.Pin_0, C24.+, C26.1, C27.1, R14.Pin_0, R15.Pin_0, IC2.12, IC2.13, IC1.16, D2.C
  CLK: ClockLED.C, R4.Pin_0, manStepLED.C, IC1.14
  N4: Q3.B, R8.Pin_1
  N5: Q3.C, Q4.B, R7.Pin_1
  N6: Q4.C, R5.Pin_1, ResetLED.A
  RES: R6.Pin_0, ResetLED.C, D8.C, D3.C, manResetLED.C, IC1.15
  N7: J9.pin1, -_GND_+1.pin1, D2.A
  N8: J9.pin5, -_GND_+1.pin5, D1.C
  -12V: C23.-, C25.1, IC2.4, D1.A
  Tre: SW3.L1, IC2.8, IC1.7
  N9: SW3.COM, D8.A
  Uno: SW3.L2, IC2.16, IC1.2
  N10: R8.Pin_0, Reset.Pin_3
  N11: R1.Pin_0, Step.Pin_3
  N12: R9.Pin_0, OI.Pin_3
  OI: R9.Pin_1, IC2.2, IC2.7, IC2.10, IC2.15
  N13: R10.Pin_0, IO1.Pin_3
  IO1: R10.Pin_1, IC2.3
  N14: R11.Pin_0, IO2.Pin_3
  IO2: R11.Pin_1, IC2.14
  N15: R12.Pin_0, IO3.Pin_3
  IO3: R12.Pin_1, IC2.11
  N16: R13.Pin_0, IO4.Pin_3
  IO4: R13.Pin_1, IC2.6
  N17: D3.A, IC1.10
  N18: R14.Pin_1, S1.1
  N19: manStepLED.A, C28.0, S1.3
  N20: R15.Pin_1, S2.1
  N21: manResetLED.A, C29.0, S2.3
  Zero: IC2.1, IC1.3
  Dos: IC2.9, IC1.4

custom parts:
  Vertical Resistor: A generic resistor (0.25W)
  3.5mm Switch Jack: Thonkiconn 3.5mm switching Jack
